// Logisim project CPU-Modified-PC.circ as structural Verilog: 6 circuits, main circuit main
module main (
  input  [3:0] in_1,
  input  in_2,
  input  in_3,
  output [7:0] out_4
);

  wire and_1_out, and_2_out, and_3_out, and_4_out, and_5_out, and_6_out, and_7_out, and_8_out, clock_1_out,
       clock_2_out, d_ff_1_q, main_1_out_4, main_2_out_2, main_2_out_3, main_2_out_4, main_2_out_5,
       main_2_out_6, main_2_out_7, main_2_out_8, main_3_out_2, main_3_out_3, main_3_out_4, main_3_out_5,
       main_3_out_6, main_3_out_7, main_3_out_8, main_4_out_2, main_4_out_3, main_4_out_4, main_4_out_5,
       main_4_out_6, main_4_out_7, main_4_out_8;
  wire [3:0] adder_1_out, multiplexer_1_out, register_1_q, yeah_1_out_21, yeah_1_out_22, yeah_1_out_23;
  wire [7:0] adder_2_out, RAM_out_5, register_2_q;

  _4BitCounter_main main_1 (
    .in_1(clock_1_out), .in_2(in_1), .in_3(in_2), .out_4(main_1_out_4));  // open: out_10, out_5, out_6, out_11, out_7, out_8, out_9
  Clock clock_1 (.out(clock_1_out));
  Multiplexer #(.width(4)) multiplexer_1 (
    .in0(4'b0000), .in1(4'b0001), .out(multiplexer_1_out), .sel(main_1_out_4));  // open: en
  Adder #(.width(4)) adder_1 (.a(multiplexer_1_out), .b(register_1_q), .out(adder_1_out));  // open: cin, cout
  and and_1 (and_1_out, clock_2_out, clock_2_out);
  Adder adder_2 (.a(register_2_q), .b(8'h7), .out(adder_2_out));  // open: cin, cout
  Register #(.width(4)) register_1 (.D(adder_1_out), .Q(register_1_q), .clk(clock_1_out));  // open: en, clr
  and and_2 (and_2_out, and_3_out, and_3_out);
  and and_3 (and_3_out, and_1_out, and_1_out);
  Register register_2 (.D(adder_2_out), .Q(register_2_q), .clk(clock_1_out));  // open: en, clr
  RAM RAM (.in_3(register_2_q), .in_1(in_3), .in_2(clock_1_out), .out_5(RAM_out_5), .in_4(register_1_q));
  _7_Segment_Display u_7_segment_display_1 (
    .g(main_2_out_2), .f(main_2_out_3), .a(main_2_out_4), .b(main_2_out_5), .e(main_2_out_8),
    .d(main_2_out_7), .c(main_2_out_6));  // open: dp
  and and_4 (and_4_out, and_2_out, and_2_out);
  Register register_3 (.D(RAM_out_5), .Q(out_4), .clk(clock_1_out));  // open: en, clr
  display_main main_2 (
    .in_1(yeah_1_out_23), .out_6(main_2_out_6), .out_7(main_2_out_7), .out_8(main_2_out_8),
    .out_2(main_2_out_2), .out_3(main_2_out_3), .out_4(main_2_out_4), .out_5(main_2_out_5));
  and and_5 (and_5_out, and_4_out, and_4_out);
  and and_6 (and_6_out, and_5_out, and_5_out);
  _7_Segment_Display u_7_segment_display_2 (
    .g(main_3_out_2), .f(main_3_out_3), .a(main_3_out_4), .b(main_3_out_5), .e(main_3_out_8),
    .d(main_3_out_7), .c(main_3_out_6));  // open: dp
  and and_7 (and_7_out, and_6_out, and_6_out);
  Yeah yeah_1 (
    .in_1(1'b0), .in_2(1'b0), .in_3(1'b0), .in_4(1'b0), .in_5(1'b0), .in_6(1'b0), .in_7(1'b0), .in_8(1'b0),
    .in_9(1'b0), .in_10(1'b0), .in_11(1'b0), .in_12(1'b0), .in_13(out_4[7]), .in_14(out_4[6]),
    .in_15(out_4[5]), .in_16(out_4[4]), .in_17(out_4[3]), .in_18(out_4[2]), .in_19(out_4[1]),
    .in_20(out_4[0]), .out_21(yeah_1_out_21), .out_22(yeah_1_out_22), .out_23(yeah_1_out_23));
  display_main main_3 (
    .in_1(yeah_1_out_22), .out_6(main_3_out_6), .out_7(main_3_out_7), .out_8(main_3_out_8),
    .out_2(main_3_out_2), .out_3(main_3_out_3), .out_4(main_3_out_4), .out_5(main_3_out_5));
  _7_Segment_Display u_7_segment_display_3 (
    .g(main_4_out_2), .f(main_4_out_3), .a(main_4_out_4), .b(main_4_out_5), .e(main_4_out_8),
    .d(main_4_out_7), .c(main_4_out_6));  // open: dp
  and and_8 (and_8_out, and_7_out, and_7_out);
  Clock clock_2 (.out(clock_2_out));
  display_main main_4 (
    .in_1(yeah_1_out_21), .out_6(main_4_out_6), .out_7(main_4_out_7), .out_8(main_4_out_8),
    .out_2(main_4_out_2), .out_3(main_4_out_3), .out_4(main_4_out_4), .out_5(main_4_out_5));
  D_Flip_Flop d_ff_1 (.clk(clock_2_out), .D(and_8_out), .Q(d_ff_1_q));  // open: Qn, preset, en, reset
endmodule

module ADD (
  input  [7:0] in_1,
  input  in_2,
  input  ITEM_5,
  input  ITEM_4,
  input  in_5,
  input  in_6,
  input  ITEM_2,
  input  in_8,
  input  in_9,
  input  in_10,
  output out_11
);

  wire and_1_out, and_2_out, and_3_out, and_4_out, clock_1_out, decoder_1_out0, decoder_1_out1,
       decoder_2_out0, decoder_2_out1;
  wire [7:0] adder_1_out_5, multiplexer_1_out, multiplexer_2_out, multiplexer_3_out, register_1_q,
       register_2_q, register_3_q, register_4_q, register_5_q;

  Multiplexer #(.width(8)) multiplexer_1 (
    .in0(in_1), .in1(register_5_q), .out(multiplexer_1_out), .sel(in_8));  // open: en
  Register register_1 (.D(multiplexer_1_out), .Q(register_1_q), .clk(and_1_out));  // open: en, clr
  and and_1 (and_1_out, decoder_1_out0, ITEM_5, clock_1_out);
  Decoder decoder_1 (.out0(decoder_1_out0), .out1(decoder_1_out1), .sel(ITEM_4));  // open: en
  Clock clock_1 (.out(clock_1_out));
  Register register_2 (.D(multiplexer_1_out), .Q(register_2_q), .clk(and_2_out));  // open: en, clr
  and and_2 (and_2_out, decoder_1_out1, ITEM_5, clock_1_out);
  Multiplexer #(.width(8)) multiplexer_2 (
    .in0(register_1_q), .in1(register_2_q), .out(multiplexer_2_out), .sel(in_5));  // open: en
  Multiplexer #(.width(8)) multiplexer_3 (
    .in0(multiplexer_1_out), .in1(multiplexer_2_out), .out(multiplexer_3_out), .sel(in_6));  // open: en
  Register register_3 (.D(multiplexer_3_out), .Q(register_3_q), .clk(and_3_out));  // open: en, clr
  and and_3 (and_3_out, clock_1_out, decoder_2_out0, decoder_2_out0);
  Decoder decoder_2 (.out0(decoder_2_out0), .out1(decoder_2_out1), .sel(ITEM_2));  // open: en
  Register register_4 (.D(multiplexer_3_out), .Q(register_4_q), .clk(and_4_out));  // open: en, clr
  and and_4 (and_4_out, clock_1_out, decoder_2_out1, decoder_2_out1);
  ADDER adder_1 (.in_1(in_2), .in_2(register_3_q), .in_3(register_4_q), .out_4(out_11), .out_5(adder_1_out_5));
  Register register_5 (.D(adder_1_out_5), .Q(register_5_q), .clk(clock_1_out));  // open: en, clr

  // Notes on the sheet:
  //   ITEM 1
  //   ITEM 3
  //   A-OUT
endmodule

module CONTROL_UNIT (
  input  [7:0] in_1,
  output out_2,
  output out_3,
  output out_4,
  output out_5,
  output out_6,
  output out_7,
  output out_8,
  output out_9,
  output out_10,
  output out_11
);

  wire _00, _01, _10, _11, add, ARG1, ARG2, CLK, DEST, INP, not_1_out, not_2_out, not_3_out, not_4_out,
       not_5_out, not_6_out, not_7_out, not_8_out, not_9_out, not_10_out, not_11_out, not_12_out, not_13_out,
       not_14_out, not_15_out, or_1_out, or_2_out, PRT, STP, SUB;
  wire [3:0] _1TK, _3TX, _4TX, adder_1_out, jmp, multiplexer_6_out, multiplexer_7_out, or_3_out;
  wire [7:0] multiplexer_3_out, multiplexer_5_out;

  // AND_Gate and_1 is placed but not wired
  Clock clock_1 (.out(CLK));
  not not_1 (not_1_out, multiplexer_5_out[2]);
  not not_2 (not_2_out, multiplexer_5_out[2]);
  not not_3 (not_3_out, multiplexer_5_out[1]);
  not not_4 (not_4_out, multiplexer_5_out[0]);
  not not_5 (not_5_out, multiplexer_5_out[3]);
  not not_6 (not_6_out, multiplexer_5_out[1]);
  and u_ADD (add, multiplexer_5_out[3], not_1_out, not_6_out, not_4_out);
  and u_SUB (SUB, not_5_out, not_2_out, not_3_out, multiplexer_5_out[0]);
  not not_7 (not_7_out, multiplexer_5_out[3]);
  not not_8 (not_8_out, multiplexer_5_out[0]);
  not not_9 (not_9_out, multiplexer_5_out[3]);
  and u_PRT (PRT, not_9_out, not_7_out, multiplexer_5_out[1], not_8_out);
  or or_1 (or_1_out, SUB, add);
  or or_2 (or_2_out, PRT, INP);
  and and_2 (out_10, not_13_out, _01);
  not not_10 (not_10_out, multiplexer_5_out[3]);
  not not_11 (not_11_out, multiplexer_5_out[3]);
  not not_12 (not_12_out, multiplexer_5_out[0]);
  and u_STP (STP, not_11_out, multiplexer_5_out[2], multiplexer_5_out[1], not_12_out);
  Multiplexer #(.width(4)) multiplexer_1 (.in0(4'b0000), .in1(4'b0100), .out(_4TX), .sel(or_1_out));  // open: en
  Multiplexer #(.width(4)) multiplexer_2 (.in0(4'b0000), .in1(4'b0001), .out(_1TK), .sel(or_2_out));  // open: en
  not not_13 (not_13_out, multiplexer_3_out[0]);
  and and_3 (out_11, multiplexer_3_out[0], _01);
  not not_14 (not_14_out, multiplexer_5_out[0]);
  not not_15 (not_15_out, multiplexer_5_out[1]);
  and u_INP (INP, not_10_out, multiplexer_5_out[2], not_15_out, not_14_out);
  Multiplexer #(.width(8)) multiplexer_3 (
    .in0({8{1'b0}}), .in1(in_1), .out({multiplexer_3_out[7:6], DEST, multiplexer_3_out[4:0]}), .sel(_01));  // open: en
  Multiplexer #(.width(4)) multiplexer_4 (.in0(4'b0000), .in1(4'b0011), .out(_3TX), .sel(_01));  // open: en
  Multiplexer #(.width(8)) multiplexer_5 (
    .in0({8{1'b0}}), .in1(in_1), .out({multiplexer_5_out[7:6], ARG2, ARG1, multiplexer_5_out[3:0]}), .sel(_00));  // open: en
  assign or_3_out = _4TX | _1TK | jmp | _3TX;  // OR_Gate or_3, 4 bits wide
  // AND_Gate and_4 is placed but not wired
  Decoder #(.select(2)) decoder_1 (.out0(_00), .out1(_01), .out2(_10), .out3(_11), .sel(in_1[7:6]));  // open: en
  Adder #(.width(4)) adder_1 (.a(4'b0011), .b(or_3_out), .out(adder_1_out));  // open: cin, cout
  _4BitCounter_main main_1 (
    .in_1(CLK), .in_2(adder_1_out), .in_3(STP), .out_10(out_2), .out_4(out_3), .out_5(out_4), .out_6(out_5),
    .out_11(out_6), .out_7(out_7), .out_8(out_8), .out_9(out_9));
  assign jmp = multiplexer_6_out | multiplexer_7_out;  // OR_Gate or_4, 4 bits wide
  Multiplexer #(.width(4)) multiplexer_6 (
    .in0(4'b0000), .in1(4'b0100), .out(multiplexer_6_out), .sel(_10));  // open: en
  Multiplexer #(.width(4)) multiplexer_7 (
    .in0(4'b0000), .in1(4'b0100), .out(multiplexer_7_out), .sel(_11));  // open: en
  Multiplexer #(.width(8)) multiplexer_8 (.in0({8{1'b0}}), .in1(in_1), .sel(_10));  // open: out, en
  Multiplexer #(.width(8)) multiplexer_9 (.in0({8{1'b0}}), .in1(in_1), .sel(_11));  // open: out, en
  // AND_Gate and_5 is placed but not wired

  // Other names for the same wires on the sheet: _1 = out_3; _2 = out_4; _3 = out_5; _4 = out_6; _5 = out_7;
  //   _6 = out_8; _7 = out_9; INSTR[7:0] = in_1; LOAD = out_10; STORE = out_11; ZERO = out_2

  // Notes on the sheet:
  //   ADDER PART
  //   MASTER_COUNTER
endmodule

module trying_counter (
  input  in_1,
  input  in_2,
  input  in_3,
  input  ITEM_2,
  input  in_5,
  input  [7:0] in_6,
  output [7:0] out_7,
  output out_8
);

  wire and_1_out, and_2_out, and_3_out, and_4_out, and_5_out, and_6_out, and_7_out, and_8_out, and_9_out,
       and_10_out, and_11_out, and_12_out, CLK, decoder_1_out0, decoder_1_out1, delay_1_out_2, FIVE, FOUR,
       ONE, or_1_out, SIX, SVN, THREE, TWO, undriven, ZERO;
  wire [3:0] adder_1_out, multiplexer_1_out, register_2_q;
  wire [7:0] adder_2_out_5, multiplexer_2_out, multiplexer_3_out, register_1_q, register_3_q, register_5_q,
       register_6_q, register_8_q, register_9_q;

  _4BitCounter_main main_1 (
    .in_1(CLK), .in_2(4'b0100), .in_3(in_1), .out_10(ZERO), .out_4(ONE), .out_5(TWO), .out_6(THREE),
    .out_11(FOUR), .out_7(FIVE), .out_8(SIX), .out_9(SVN));
  Multiplexer #(.width(4)) multiplexer_1 (
    .in0(4'b0000), .in1(4'b0001), .out(multiplexer_1_out), .sel(THREE));  // open: en
  Register register_1 (.D(in_6), .Q(register_1_q), .clk(and_1_out));  // open: en, clr
  and and_1 (and_1_out, CLK, ONE);
  Adder #(.width(4)) adder_1 (.a(multiplexer_1_out), .b(register_2_q), .out(adder_1_out));  // open: cin, cout
  Register #(.width(4)) register_2 (.D(adder_1_out), .Q(register_2_q), .clk(CLK));  // open: en, clr
  Register register_3 (.D(register_1_q), .Q(register_3_q), .clk(and_2_out));  // open: en, clr
  and and_2 (and_2_out, CLK, TWO);
  Register register_4 (.D(register_3_q), .clk(and_3_out));  // open: en, Q, clr
  and and_3 (and_3_out, CLK, THREE);
  and and_4 (and_4_out, FOUR, CLK);
  and and_5 (and_5_out, decoder_1_out0, and_4_out, CLK);
  Clock clock_1 (.out(CLK));
  Register register_5 (.D(register_9_q), .Q(register_5_q), .clk(and_5_out));  // open: en, clr
  and and_6 (and_6_out, decoder_1_out1, and_4_out, CLK);
  Decoder decoder_1 (.out0(decoder_1_out0), .out1(decoder_1_out1), .sel(in_3));  // open: en
  T_Flip_Flop t_ff_1 (.clk(CLK), .T(undriven));  // open: Q, Qn, preset, reset, en
  Register register_6 (.D(register_9_q), .Q(register_6_q), .clk(and_6_out));  // open: en, clr
  Multiplexer #(.width(8)) multiplexer_2 (
    .in0(register_5_q), .in1(register_6_q), .out(multiplexer_2_out), .sel(or_1_out));  // open: en
  or or_1 (or_1_out, and_7_out, and_9_out, and_8_out);
  and and_7 (and_7_out, ONE, in_3);
  and and_8 (and_8_out, TWO, in_5);
  and and_9 (and_9_out, ZERO, in_3);
  and and_10 (and_10_out, CLK, ONE);
  Multiplexer #(.width(8)) multiplexer_3 (
    .in0(register_9_q), .in1(multiplexer_2_out), .out(multiplexer_3_out), .sel(1'b1));  // open: en
  Register register_7 (.D(multiplexer_3_out), .Q(out_7), .clk(and_10_out));  // open: en, clr
  and and_11 (and_11_out, delay_1_out_2, TWO);
  DELAY delay_1 (.in_1(CLK), .out_2(delay_1_out_2));
  ADDER adder_2 (.in_1(in_2), .in_2(out_7), .in_3(register_8_q), .out_4(out_8), .out_5(adder_2_out_5));
  Register register_8 (.D(multiplexer_3_out), .Q(register_8_q), .clk(and_11_out));  // open: en, clr
  Register register_9 (.D(adder_2_out_5), .Q(register_9_q), .clk(and_12_out));  // open: en, clr
  and and_12 (and_12_out, CLK, THREE);
  T_Flip_Flop t_ff_2 (.clk(and_12_out), .T(1'b1));  // open: Q, Qn, preset, reset, en

  // Other names for the same wires on the sheet: ARG1 = in_3; ARG2 = in_5

  // Notes on the sheet:
  //   NOTE: ADD AND GATE IN TIMER
  //   ITEM 4
  //   ITEM 1
  //   ITEM 3
  //   A-OUT
endmodule

module DELAY (
  input  in_1,
  output out_2
);

  wire and_1_out, and_2_out, and_3_out, and_4_out, and_5_out, and_6_out, and_7_out, and_8_out, and_9_out,
       and_10_out, and_11_out, and_12_out, and_13_out, and_14_out, and_15_out;

  and and_1 (and_1_out, in_1, in_1);
  and and_2 (and_2_out, and_3_out, and_3_out);
  and and_3 (and_3_out, and_1_out, and_1_out);
  and and_4 (and_4_out, and_2_out, and_2_out);
  and and_5 (and_5_out, and_4_out, and_4_out);
  and and_6 (and_6_out, and_5_out, and_5_out);
  and and_7 (and_7_out, and_6_out, and_6_out);
  and and_8 (and_8_out, and_7_out, and_7_out);
  and and_9 (and_9_out, and_8_out, and_8_out);
  and and_10 (and_10_out, and_9_out, and_9_out);
  and and_11 (and_11_out, and_10_out, and_10_out);
  and and_12 (and_12_out, and_11_out, and_11_out);
  and and_13 (and_13_out, and_12_out, and_12_out);
  and and_14 (and_14_out, and_13_out, and_13_out);
  and and_15 (and_15_out, and_14_out, and_14_out);
  and and_16 (out_2, and_15_out, and_15_out);
endmodule

module _8_bit_register (
  input  [7:0] in_1,
  input  in_2,
  output [7:0] out_3
);

  D_Flip_Flop d_ff_1 (.clk(in_2), .D(in_1[7]), .Q(out_3[7]));  // open: Qn, preset, en, reset
  D_Flip_Flop d_ff_2 (.clk(in_2), .D(in_1[6]), .Q(out_3[6]));  // open: Qn, preset, en, reset
  D_Flip_Flop d_ff_3 (.clk(in_2), .D(in_1[5]), .Q(out_3[5]));  // open: Qn, preset, en, reset
  D_Flip_Flop d_ff_4 (.clk(in_2), .D(in_1[4]), .Q(out_3[4]));  // open: Qn, preset, en, reset
  D_Flip_Flop d_ff_5 (.clk(in_2), .D(in_1[3]), .Q(out_3[3]));  // open: Qn, preset, en, reset
  D_Flip_Flop d_ff_6 (.clk(in_2), .D(in_1[2]), .Q(out_3[2]));  // open: Qn, preset, en, reset
  D_Flip_Flop d_ff_7 (.clk(in_2), .D(in_1[1]), .Q(out_3[1]));  // open: Qn, preset, en, reset
  D_Flip_Flop d_ff_8 (.clk(in_2), .D(in_1[0]), .Q(out_3[0]));  // open: Qn, preset, en, reset
endmodule
